# Fritzing sketch EEI-Stopwatch (saved by Fritzing 0.9.10b)
# 18650 Li-ion Battery: CC-BY Dr Kristofer Chan, King's College London/Remote-research.org
breadboards: 1

parts:
  S1 = Pushbutton [package="[SMD]"]
  S2 = Pushbutton [package="[SMD]"]
  R1 = Resistor [tolerance=±5% power=0.25 resistance=22k package=THT]
  R2 = Resistor [tolerance=±5% power=0.25 resistance=22k package=THT]
  Part1 = Arduino Nano (Rev3.0) (ICSP)
  4-digit1 = 4-Digit 7-segment LED Display [package=THT]
  VL53L0X1 = VL53L0X ToF laser distance sensor [package=THT]
  S3 = SWITCH_SPDT [package=kps-1290]
  BAT1 = 18650 Li-ion Battery [package=battery-18650]
  M1 = MT3608 Module
  M2 = TP4056 Module [part_number=HW-107]

nets:
  GND: S1.Pin_1, S1.Pin_2, S2.Pin_1, S2.Pin_2, Part1.GND, 4-digit1.GND, VL53L0X1.GND, M1.pin4
  N1: S1.Pin_3, S1.Pin_4, R1.Pin_0
  N2: S2.Pin_3, S2.Pin_4, R1.Pin_1, R2.Pin_0
  N3: R2.Pin_1, Part1.A3
  N4: Part1.D2, 4-digit1.DIO
  N5: Part1.D3, 4-digit1.CLK
  5V: Part1.5V, 4-digit1.5V, VL53L0X1.VIN, M1.pin3
  N6: Part1.A5, VL53L0X1.SCL
  N7: Part1.A4, VL53L0X1.SDA
  N8: S3.P, M1.pin2
  N9: S3.S, M2.OUT-#4
  N10: BAT1.-, M2.BAT-
  N11: BAT1.+, M2.BAT+
  N12: M1.pin1, M2.OUT-#1

custom parts:
  4-Digit 7-segment LED Display: A 4-digit 7-segments LED display driven by a TM1637 IC via 1-wire protocol.
  VL53L0X ToF laser distance sensor: Time of Flight laser distance sensor VL53L0X.
  18650 Li-ion Battery: 18650 li-ion Battery Standard 18650 battery with interactive connectors Creative Common Attribution 4.0 International (CC-BY 4.0) license. Any use of this part requires attribution of Dr Kristofer Chan, Department of Geography, King's College London. Contact kristofer.chan [at] kcl.ac.uk OR kris [at] remote-research.org for further information.
  MT3608 Module: MT3608 Boost Converter Module Links: Aerosemi MT3608 2A Step Up Converter datasheet
  TP4056 Module: TP4056 Lithium Battery Charge Management Module Links: TP4056 website
